# Fritzing sketch fmtrans (saved by Fritzing 0.9.3b)
circuit board: 8.46667cm x 5.64444cm
breadboards: 1

parts:
  S_Trig = Hex Inverter Schmitt Trigger SN74HC14 [package="DIP (Dual Inline)"]
  R1 = Resistor [tolerance=±5% resistance=220 package=THT]
  R2 = Resistor [tolerance=±5% resistance=220 package=THT]
  LED1 = LED - 5mm [color="Red (633nm)" package="5 mm [THT]"]
  C1 = Ceramic Capacitor [capacitance=100nF package="100 mil [THT, multilayer]"]
  C3 = Ceramic Capacitor [capacitance=100nF package="100 mil [THT, multilayer]"]
  C2 = Ceramic Capacitor [capacitance=100nF package="100 mil [THT, multilayer]"]
  ANT1 = Antenna
  Batt = Battery block 9V
  J2 = Screw terminal - 2 pins [package=THT]
  MIC = Microphone
  7805 = Voltage Regulator [package=to-220-alt]

nets:
  N1: S_Trig.1A, S_Trig.1Y, S_Trig.2Y, S_Trig.3Y, C2.1, ANT1.antenna_lead
  N2: S_Trig.3A, C1.1
  GND: S_Trig.GND, LED1.cathode, C3.0, C2.0, Batt.-, 7805.GND
  N3: S_Trig.VCC, R1.Pin_0, R2.Pin_0, C3.1, 7805.OUT
  N4: R1.Pin_1, C1.0, J2.pin1, MIC.pin1
  N5: R2.Pin_1, LED1.anode
  N6: Batt.+, 7805.IN
  N7: J2.pin2, MIC.pin2

notes:
  FM Tansmitter, FM transmitter cicuit without coil                         github.com/srihariash999, 1.0
  FM Transmitter - github.com/srihariash999
  S.Trig
  C1
  Ant
  J1
  C2
  Mic
  R1
  7805
  LED
  R2
  C3
  Batt
